# Fritzing sketch Magnetic_Counter_Circuit (saved by Fritzing 0.9.3b)
breadboards: 2

parts:
  Part1 = Arduino Uno (Rev3)
  U1 = 7-SEGMENT-DISPLAY-1_-RED [package=7-segment-1_pth]
  IC1 = IC, DIP package, 16 pins [chip_label="BDC Decoder"]
  IC2 = IC, DIP package, 16 pins [chip_label="BDC Decoder"]
  IC3 = IC, DIP package, 16 pins [chip_label="BDC Decoder"]
  IC4 = IC, DIP package, 16 pins [chip_label="BDC Decoder"]
  R1 = Resistor [tolerance=±5% resistance=390 package=THT]
  R2 = Resistor [tolerance=±5% resistance=390 package=THT]
  R3 = Resistor [tolerance=±5% resistance=390 package=THT]
  R4 = Resistor [tolerance=±5% resistance=390 package=THT]
  R5 = Resistor [tolerance=±5% resistance=390 package=THT]
  R6 = Resistor [tolerance=±5% resistance=390 package=THT]
  R7 = Resistor [tolerance=±5% resistance=390 package=THT]
  U2 = 7-SEGMENT-DISPLAY-1_-RED [package=7-segment-1_pth]
  R8 = Resistor [tolerance=±5% resistance=390 package=THT]
  R9 = Resistor [tolerance=±5% resistance=390 package=THT]
  R10 = Resistor [tolerance=±5% resistance=390 package=THT]
  R11 = Resistor [tolerance=±5% resistance=390 package=THT]
  R12 = Resistor [tolerance=±5% resistance=390 package=THT]
  R13 = Resistor [tolerance=±5% resistance=390 package=THT]
  R14 = Resistor [tolerance=±5% resistance=390 package=THT]
  U3 = 7-SEGMENT-DISPLAY-1_-RED [package=7-segment-1_pth]
  R15 = Resistor [tolerance=±5% resistance=390 package=THT]
  R16 = Resistor [tolerance=±5% resistance=390 package=THT]
  R17 = Resistor [tolerance=±5% resistance=390 package=THT]
  R18 = Resistor [tolerance=±5% resistance=390 package=THT]
  R19 = Resistor [tolerance=±5% resistance=390 package=THT]
  R20 = Resistor [tolerance=±5% resistance=390 package=THT]
  R21 = Resistor [tolerance=±5% resistance=390 package=THT]
  U4 = 7-SEGMENT-DISPLAY-1_-RED [package=7-segment-1_pth]
  R22 = Resistor [tolerance=±5% resistance=390 package=THT]
  R23 = Resistor [tolerance=±5% resistance=390 package=THT]
  R24 = Resistor [tolerance=±5% resistance=390 package=THT]
  R25 = Resistor [tolerance=±5% resistance=390 package=THT]
  R26 = Resistor [tolerance=±5% resistance=390 package=THT]
  R27 = Resistor [tolerance=±5% resistance=390 package=THT]
  R28 = Resistor [tolerance=±5% resistance=390 package=THT]
  S1 = Reed switch [package=THT]
  R29 = Resistor [tolerance=±5% resistance=10k package=THT]

nets:
  N1: Part1.D8, IC1.pin4
  N2: Part1.D9_PWM, IC2.pin4
  N3: Part1.D10_PWM/SS, IC3.pin4
  N4: Part1.D11_PWM/MOSI, IC4.pin4
  N5: Part1.D12/MISO, S1.pin_1, R29.Pin_0
  N6: Part1.D2, IC1.pin7, IC2.pin7, IC3.pin7, IC4.pin7
  N7: Part1.D3_PWM, IC1.pin1, IC2.pin1, IC3.pin1, IC4.pin1
  N8: Part1.D4, IC1.pin2, IC2.pin2, IC3.pin2, IC4.pin2
  N9: Part1.D5_PWM, IC1.pin6, IC2.pin6, IC3.pin6, IC4.pin6
  N10: Part1.D6_PWM, IC1.pin5, IC2.pin5, IC3.pin5, IC4.pin5
  N11: Part1.D7, IC1.pin3, IC2.pin3, IC3.pin3, IC4.pin3
  N12: Part1.5V, U1.G1, IC1.pin16, IC2.pin16, IC3.pin16, IC4.pin16, U2.G1, U3.G1, U4.G1, R29.Pin_1
  N13: Part1.GND, IC1.pin8, IC2.pin8, IC3.pin8, IC4.pin8, S1.pin_2
  N14: U1.E, R7.Pin_0
  N15: U1.D, R6.Pin_0
  N16: U1.C, R5.Pin_0
  N17: U1.B, R4.Pin_0
  N18: U1.A, R3.Pin_0
  N19: U1.F, R1.Pin_0
  N20: U1.G, R2.Pin_0
  N21: IC1.pin9, R7.Pin_1
  N22: IC1.pin10, R6.Pin_1
  N23: IC1.pin11, R5.Pin_1
  N24: IC1.pin12, R4.Pin_1
  N25: IC1.pin13, R3.Pin_1
  N26: IC1.pin14, R2.Pin_1
  N27: IC1.pin15, R1.Pin_1
  N28: IC2.pin9, R14.Pin_1
  N29: IC2.pin10, R9.Pin_1
  N30: IC2.pin11, R13.Pin_1
  N31: IC2.pin12, R11.Pin_1
  N32: IC2.pin13, R12.Pin_1
  N33: IC2.pin14, R8.Pin_1
  N34: IC2.pin15, R10.Pin_1
  N35: IC3.pin9, R21.Pin_1
  N36: IC3.pin10, R16.Pin_1
  N37: IC3.pin11, R20.Pin_1
  N38: IC3.pin12, R18.Pin_1
  N39: IC3.pin13, R19.Pin_1
  N40: IC3.pin14, R15.Pin_1
  N41: IC3.pin15, R17.Pin_1
  N42: IC4.pin9, R28.Pin_1
  N43: IC4.pin10, R23.Pin_1
  N44: IC4.pin11, R27.Pin_1
  N45: IC4.pin12, R25.Pin_1
  N46: IC4.pin13, R26.Pin_1
  N47: IC4.pin14, R22.Pin_1
  N48: IC4.pin15, R24.Pin_1
  N49: U2.E, R14.Pin_0
  N50: U2.D, R9.Pin_0
  N51: U2.C, R13.Pin_0
  N52: U2.B, R11.Pin_0
  N53: U2.A, R12.Pin_0
  N54: U2.F, R10.Pin_0
  N55: U2.G, R8.Pin_0
  N56: U3.E, R21.Pin_0
  N57: U3.D, R16.Pin_0
  N58: U3.C, R20.Pin_0
  N59: U3.B, R18.Pin_0
  N60: U3.A, R19.Pin_0
  N61: U3.F, R17.Pin_0
  N62: U3.G, R15.Pin_0
  N63: U4.E, R28.Pin_0
  N64: U4.D, R23.Pin_0
  N65: U4.C, R27.Pin_0
  N66: U4.B, R25.Pin_0
  N67: U4.A, R26.Pin_0
  N68: U4.F, R24.Pin_0
  N69: U4.G, R22.Pin_0
