# Fritzing sketch Single_Digit_Circuit (saved by Fritzing 0.9.3b)
breadboards: 2

parts:
  Part1 = Arduino Uno (Rev3)
  U1 = 7-SEGMENT-DISPLAY-1_-RED [package=7-segment-1_pth]
  IC1 = IC, DIP package, 16 pins [chip_label="BDC Decoder"]
  R1 = Resistor [tolerance=±5% resistance=390 package=THT]
  R2 = Resistor [tolerance=±5% resistance=390 package=THT]
  R3 = Resistor [tolerance=±5% resistance=390 package=THT]
  R4 = Resistor [tolerance=±5% resistance=390 package=THT]
  R5 = Resistor [tolerance=±5% resistance=390 package=THT]
  R6 = Resistor [tolerance=±5% resistance=390 package=THT]
  R7 = Resistor [tolerance=±5% resistance=390 package=THT]

nets:
  N1: Part1.D8, IC1.pin4
  N2: Part1.D2, IC1.pin7
  N3: Part1.D3_PWM, IC1.pin1
  N4: Part1.D4, IC1.pin2
  N5: Part1.D5_PWM, IC1.pin6
  N6: Part1.D6_PWM, IC1.pin5
  N7: Part1.D7, IC1.pin3
  N8: Part1.5V, U1.G1, IC1.pin16
  N9: Part1.GND, IC1.pin8
  N10: IC1.pin9, R7.Pin_1
  N11: IC1.pin10, R6.Pin_1
  N12: IC1.pin11, R5.Pin_1
  N13: IC1.pin12, R4.Pin_1
  N14: IC1.pin13, R3.Pin_1
  N15: IC1.pin14, R2.Pin_1
  N16: IC1.pin15, R1.Pin_1
